# Fritzing sketch schematic_binary_counter (saved by Fritzing 0.9.3b)
breadboards: 1

parts:
  Part1 = Arduino Uno (Rev3) - ICSP
  R1 = Resistor [tolerance=±5% resistance=330 package=THT]
  R2 = Resistor [tolerance=±5% resistance=330 package=THT]
  R3 = Resistor [tolerance=±5% resistance=330 package=THT]
  R4 = Resistor [tolerance=±5% resistance=330 package=THT]
  LED1 = smd LED [color="Red (633nm)" package="0603 [SMD]"]
  LED2 = smd LED [color="Red (633nm)" package="0603 [SMD]"]
  LED3 = smd LED [color="Red (633nm)" package="0603 [SMD]"]
  LED4 = smd LED [color="Red (633nm)" package="0603 [SMD]"]

nets:
  N1: Part1.GND, LED1.cathode, LED2.cathode, LED3.cathode, LED4.cathode
  N2: Part1.D2, R1.Pin_1
  N3: Part1.D3_PWM, R2.Pin_1
  N4: Part1.D4, R3.Pin_1
  N5: Part1.D5_PWM, R4.Pin_1
  N6: R1.Pin_0, LED1.anode
  N7: R2.Pin_0, LED2.anode
  N8: R3.Pin_0, LED3.anode
  N9: R4.Pin_0, LED4.anode
